// Logisim project sagui.circ as structural Verilog: 4 circuits, main circuit main
module main (
);

  wire alu_1_zero;
  wire [7:0] PC_q;

  Register PC (.Q(PC_q));  // open: D, en, clk, clr
  ROM Instrucoes (.addr(PC_q));  // open: data
  Adder adder_1 (.a(PC_q), .b(8'h4));  // open: out, cin, cout
  banco_reg banco_reg_1 ();  // open: ReadRegister1, WriteData, ReadRegister2, WriteRegister, RegWrite, ReadData1, ReadData2
  Bit_Extender #(.out_width(8)) bit_extender_1 ();  // open: in, out
  RAM ram_1 (.ld(alu_1_zero));  // open: addr, data, sel, clk, clr
  ALU alu_1 (.Zero(alu_1_zero));  // open: Operand1, Operand2, ALUOp, Result
endmodule

module banco_reg (
  input  [1:0] ReadRegister1,
  input  [7:0] WriteData,
  input  [1:0] ReadRegister2,
  input  [1:0] WriteRegister,
  input  RegWrite,
  output [7:0] ReadData1,
  output [7:0] ReadData2
);

  wire Clk, demultiplexer_2_out0, demultiplexer_2_out1, demultiplexer_2_out2, demultiplexer_2_out3;
  wire [7:0] demultiplexer_1_out0, demultiplexer_1_out1, demultiplexer_1_out2, demultiplexer_1_out3,
       register_1_q, register_2_q, register_3_q, register_4_q;

  Clock clock_1 (.out(Clk));
  Demultiplexer #(.select(2), .width(8)) demultiplexer_1 (
    .out0(demultiplexer_1_out0), .out1(demultiplexer_1_out1), .out2(demultiplexer_1_out2),
    .out3(demultiplexer_1_out3), .in(WriteData), .sel(WriteRegister));
  Demultiplexer #(.select(2)) demultiplexer_2 (
    .out0(demultiplexer_2_out0), .out1(demultiplexer_2_out1), .out2(demultiplexer_2_out2),
    .out3(demultiplexer_2_out3), .in(RegWrite), .sel(WriteRegister));
  Register register_1 (.D(demultiplexer_1_out0), .en(demultiplexer_2_out0), .clk(Clk), .Q(register_1_q));  // open: clr
  Register register_2 (.D(demultiplexer_1_out1), .en(demultiplexer_2_out1), .clk(Clk), .Q(register_2_q));  // open: clr
  Register register_3 (.D(demultiplexer_1_out2), .en(demultiplexer_2_out2), .clk(Clk), .Q(register_3_q));  // open: clr
  Register register_4 (.D(demultiplexer_1_out3), .en(demultiplexer_2_out3), .clk(Clk), .Q(register_4_q));  // open: clr
  Multiplexer #(.select(2), .width(8)) multiplexer_1 (
    .in0(register_1_q), .in1(register_2_q), .in2(register_3_q), .in3(register_4_q), .out(ReadData1),
    .sel(ReadRegister1));
  Multiplexer #(.select(2), .width(8)) multiplexer_2 (
    .in0(register_1_q), .in1(register_2_q), .in2(register_3_q), .in3(register_4_q), .out(ReadData2),
    .sel(ReadRegister2));
endmodule

module ALU (
  input  [7:0] Operand1,
  input  [7:0] Operand2,
  input  [2:0] ALUOp,
  output Zero,
  output [7:0] Result
);

  wire [7:0] adder_1_out, and_1_out, not_1_out, shifter_1_out, shifter_2_out, subtractor_1_out;

  Adder adder_1 (.a(Operand1), .b(Operand2), .out(adder_1_out));  // open: cin, cout
  Subtractor subtractor_1 (.a(Operand1), .b(Operand2), .out(subtractor_1_out));  // open: bin, bout
  assign and_1_out = Operand1 & Operand2;  // AND_Gate and_1, 8 bits wide
  assign and_1_out = Operand1 | Operand2;  // OR_Gate or_1, 8 bits wide
  assign not_1_out = ~Operand1;  // NOT_Gate not_1, 8 bits wide
  Shifter shifter_1 (.in(Operand1), .\dist (Operand2[2:0]), .out(shifter_1_out));
  Shifter #(.shift("lr")) shifter_2 (.in(Operand1), .\dist (Operand2[2:0]), .out(shifter_2_out));
  Multiplexer #(.select(3), .width(8)) multiplexer_1 (
    .in0(adder_1_out), .in1(subtractor_1_out), .in2(and_1_out), .in3(and_1_out), .in4(not_1_out),
    .in5(shifter_1_out), .in6(shifter_2_out), .out(Result), .sel(ALUOp));  // open: in7
  IsZero iszero_1 (.Value(Result), .Result(Zero));
endmodule

module IsZero (
  input  [7:0] Value,
  output Result
);

  and and_1 (Result, 1'b1, ~Value[0], ~Value[1], ~Value[2], ~Value[3], ~Value[4], ~Value[5], ~Value[6], ~Value[7]);  // AND_Gate
endmodule
